# Fritzing sketch BME201Fritz (saved by Fritzing 0.9.3b)
breadboards: 1

parts:
  Part1 = Arduino Uno (Rev3)
  LED1 = 7-SEGMENT-4DIGIT-YOUNGSUN [package=7-segment-4digit-youngsun]
  R1 = Resistor [tolerance=±5% resistance=220 package=THT]
  R2 = Resistor [tolerance=±5% resistance=220 package=THT]
  R3 = Resistor [tolerance=±5% resistance=220 package=THT]
  R4 = Resistor [tolerance=±5% resistance=220 package=THT]
  R5 = Resistor [tolerance=±5% resistance=220 package=THT]
  R6 = Resistor [tolerance=±5% resistance=220 package=THT]
  R7 = Resistor [tolerance=±5% resistance=220 package=THT]
  R8 = Resistor [tolerance=±5% resistance=220 package=THT]
  Part2 = SparkFun_Beefcake_Relay_Control_Kit
  microSD_Transflash1 = SparkFun - microSD Transflash
  Part3 = Bi-Directional Logic Level Converter [part_number=BOB-12009]  # not connected

nets:
  N1: Part1.A1, Part2.RELAY
  N2: Part1.A2, LED1.DIG1
  N3: Part1.A3, LED1.DIG2
  N4: Part1.A4/SDA, LED1.COL-A
  N5: Part1.A5/SCL, LED1.DIG3
  N6: Part1.D8, R2.Pin_1
  N7: Part1.D9_PWM, R1.Pin_1
  GND: Part1.GND, Part2.GND, microSD_Transflash1.GND
  N8: Part1.D2, R8.Pin_1
  N9: Part1.D3_PWM, R5.Pin_1
  N10: Part1.D4, R7.Pin_1
  N11: Part1.D5_PWM, R6.Pin_1
  N12: Part1.D6_PWM, R3.Pin_1
  N13: Part1.D7, R4.Pin_1
  3V3: Part1.3V3, microSD_Transflash1.VCC
  5V: Part1.5V, Part2.VCC
  N14: LED1.D, R6.Pin_0
  N15: LED1.E, R3.Pin_0
  N16: LED1.DP, R1.Pin_0
  N17: LED1.F, R4.Pin_0
  N18: LED1.C, R7.Pin_0
  N19: LED1.A, R8.Pin_0
  N20: LED1.G, R2.Pin_0
  N21: LED1.B, R5.Pin_0

notes:
  temperature sensing thermistor circuit
  3.3v
  Ground
  5v

custom parts:
  Bi-Directional Logic Level Converter: Description: If you've ever tried to connect a 3.3V device to a 5V system, you know what a challenge it can be. The SparkFun bi-directional logic level converter is a small device that safely steps down 5V signals to 3.3V AND steps up 3.3V to 5V at the same time. This level converter also works with 2.8V and 1.8V devices. What really separates this Logic level converter from our previous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

// code stored in the sketch: bme201fritzing.ino
/*! \file 
 * BME 201
 Victoria Trantow
 3/10/18
 This program reads in an ADC value, converts that ADC value to voltage and then temperature 
 based on the thermistor resistance/temperature calibration,displays that temperature on 
 the LCD display, records the temperature (very 1/3 sec) onto an SD card, and either 
 turn the heating element on or off through controlling the beefcake based on the temperature.*/

 

//Variable initializations
const uint8_t aIn = A0; //  AnalogRead to Serial
#include <SD.h> //SD card
File myFile; //!< The name of the variable that references the file you wish to save to
const int CS = 10; //Need to physically connect the others, but not declare variables
/*SS pin to CS pin
MOSI pin to DI
MISO pin to DO
SCK pin to SCK pin*/


 /*Output pin assignments. These correspond to the 7 segment display as well as the heating element connection.
 A generic unsigned integer can represent any number between 0 and 2^32-1.
 You can use an 8 bit uint8_t to represent up any value 0-255 which is more
 appropriate for pins and lcd digits.*/
 
 const uint8_t heatelement = A1;
 const uint8_t segA = 2;  //!< Output pin connected to segment A of the 7 seg display.
const uint8_t segB = 3; 
const uint8_t segC = 4;
const uint8_t segD = 5;
const uint8_t segE = 6;
const uint8_t segF = 7;
const uint8_t segG = 8;
const uint8_t DECIMAL = 9;
const uint8_t d1 = A2;
const uint8_t d2 = A3;
const uint8_t d3 = A4;
const uint8_t d4 = A5;

 /* Function prototypes: new functions either need to be defined or declared 
  using a prototype before using them. I am putting function prototypes at the
  beginning before loop and main, and they will be called upon during the loop()*/
void return_digits_to_display(double somenumber, uint8_t mydigits[4]);
void displayDigit(uint8_t digit);
void displayNumber(double value);

/* This returns the four digits to display.
 * param [in] somenumber: floating point number to convert into digits.
 * param [out] digits: array of four digits to represent the double.*/
void return_digits_to_display(double somenumber, uint8_t mydigits[4]){
     /* example for proof of concept: 84.65
     since the array is of integers, reassigning double values to int will just
     eliminate the digits after the decimal place. I'm using this and some basic
     algebra to my advantage to separate the double into 4 separate digits.*/
  if ((100.00 > somenumber) && (0.00 <= somenumber)) {
    mydigits[0] = somenumber/10; //8.465 --> 8
    mydigits[1] = (somenumber - mydigits[0]*10); // 84.65 - 80, 4
    mydigits[2] = (somenumber - (mydigits[0]*10 + mydigits[1]))*10; //84.65-84, *10, 6
    mydigits[3] = (somenumber + .005 - (mydigits[0]*10 + mydigits[1] + mydigits[2]*.1))*100; //84.65 - 84.6, *100, 5  
    //to verify:
    Serial.println(mydigits[0]);
    Serial.println(mydigits[1]);
    Serial.println(mydigits[2]);
    Serial.println(mydigits[3]);    
  }else{
    Serial.println("return_digits_to_display() invalid input.");
    mydigits[0] = 0;
    mydigits[1] = 0;
    mydigits[2] = 0;
    mydigits[3] = 0;
  }  
}

/*Takes a single unsigned integer digit and displays it on the LCD,
  param [in] digit: the value to display on the LCD. 
  Low corresponds with being on, high with off for this
  due to voltage drop difference for LEDs. */
void displayDigit(uint8_t digit){
  digitalWrite(DECIMAL, HIGH); //turns off the decimal place
  //switch works so that if digit is equal to the case, that case will proceed.
  switch(digit){
   case 0:   //To display 0, we turn on all segments except for segment G
      digitalWrite(segA, LOW);
      digitalWrite(segB, LOW);
      digitalWrite(segC, LOW);
      digitalWrite(segD, LOW);
      digitalWrite(segE, LOW);
      digitalWrite(segF, LOW);
      digitalWrite(segG, HIGH);
      break;
  case 1:
      digitalWrite(segA, HIGH);
      digitalWrite(segB, HIGH);
      digitalWrite(segC, HIGH);
      digitalWrite(segD, HIGH);
      digitalWrite(segE, LOW);
      digitalWrite(segF, LOW);
      digitalWrite(segG, HIGH);
      break;
  case 2:
      digitalWrite(segA, LOW);
      digitalWrite(segB, LOW);
      digitalWrite(segC, HIGH);
      digitalWrite(segD, LOW);
      digitalWrite(segE, LOW);
      digitalWrite(segF, HIGH);
      digitalWrite(segG, LOW);
      break;
  case 3:
      digitalWrite(segA, LOW);
      digitalWrite(segB, LOW);
      digitalWrite(segC, LOW);
      digitalWrite(segD, LOW);
      digitalWrite(segE, HIGH);
      digitalWrite(segF, HIGH);
      digitalWrite(segG, LOW);
      break;
  case 4:
      digitalWrite(segA, HIGH);
      digitalWrite(segB, LOW);
      digitalWrite(segC, LOW);
      digitalWrite(segD, HIGH);
      digitalWrite(segE, HIGH);
      digitalWrite(segF, LOW);
      digitalWrite(segG, LOW);
      break;
  case 5:
      digitalWrite(segA, LOW);
      digitalWrite(segB, HIGH);
      digitalWrite(segC, LOW);
      digitalWrite(segD, LOW);
      digitalWrite(segE, HIGH);
      digitalWrite(segF, LOW);
      digitalWrite(segG, LOW);
      break;
  case 6:
      digitalWrite(segA, LOW);
      digitalWrite(segB, HIGH);
      digitalWrite(segC, LOW);
      digitalWrite(segD, LOW);
      digitalWrite(segE, LOW);
      digitalWrite(segF, LOW);
      digitalWrite(segG, LOW);
      break;
   case 7:
      digitalWrite(segA, LOW);
      digitalWrite(segB, LOW);
      digitalWrite(segC, LOW);
      digitalWrite(segD, HIGH);
      digitalWrite(segE, HIGH);
      digitalWrite(segF, HIGH);
      digitalWrite(segG, HIGH);
      break;
  case 8:
      digitalWrite(segA, LOW);
      digitalWrite(segB, LOW);
      digitalWrite(segC, LOW);
      digitalWrite(segD, LOW);
      digitalWrite(segE, LOW);
      digitalWrite(segF, LOW);
      digitalWrite(segG, LOW);
      break;
  case 9:
      digitalWrite(segA, LOW);
      digitalWrite(segB, LOW);
      digitalWrite(segC, LOW);
      digitalWrite(segD, LOW);
      digitalWrite(segE, HIGH);
      digitalWrite(segF, LOW);
      digitalWrite(segG, LOW);
      break;
  default:
    Serial.println("displayDigit() invalid digit.");
    Serial.println(digit);
    break;
  }}
/* This takes a double, and refers to return_digits_to_display() function, 
 *  in order to change this double into an integer array. Then, it steps 
 *  through a for loop, at values 0,1,2,3. It's set up so that each [0 1 2 3]
 *  will correspond to a digit of the physical display, and it also corresponds 
 *  to that index in the int array of the double. So, the digit will be displayed
 *  in the correct place, and in between each loop all the places get turned off.
 *  This function gets called in the main loop, rapidly, so the number will 
 *  appear to constantly be displayed.
*/
void displayNumber(double value) {
  uint8_t d;
  uint8_t mydigits[4];
  /*Convert the floating point value into four digits.*/
  return_digits_to_display(value, mydigits);
   /*Paint each digit*/
  for(d = 0; d <4; d++) {
    //Turn on a single digit.
    displayDigit(mydigits[d]); //Turn on the correct segments for this digit.
    switch(d) {
    case 0:
      digitalWrite(d1, HIGH);
      break;
    case 1:
      digitalWrite(DECIMAL, LOW); //We want decimal to occur after the 2nd digit for the temp
      digitalWrite(d2, HIGH);
      break;
    case 2:
      digitalWrite(d3, HIGH);
      break;
    case 3:
      digitalWrite(d4, HIGH);
      break;
    }
     delayMicroseconds(10); //Display this digit for 10 microseconds)
    //Turn off all digits.
    digitalWrite(d1, LOW);
    digitalWrite(d2, LOW);
    digitalWrite(d3, LOW);
    digitalWrite(d4, LOW);
  } // for (each LED digit)
} 

  

void setup() {

    Serial.begin(9600);
    pinMode(d1, OUTPUT);
    pinMode(d2, OUTPUT);
    pinMode(d3, OUTPUT);
    pinMode(d4, OUTPUT);
    pinMode(segA, OUTPUT);
    pinMode(segB, OUTPUT);
    pinMode(segC, OUTPUT);
    pinMode(segD, OUTPUT);
    pinMode(segE, OUTPUT);
    pinMode(segF, OUTPUT);
    pinMode(segG, OUTPUT);
    pinMode(DECIMAL, OUTPUT);
    SD.begin(CS); //initializes CS pin for SD card writing

    pinMode(heatelement, OUTPUT);
}

double display_me = 0; // Initialize value to display in main loop

void loop() {  

     
     static unsigned long loop_count = 0;
     const double lowtemp = 36.0; // Low and hightemp limits are not changed so declare them as const. 
     const double hightemp = 38.0;
  
      float sensorValue = analogRead(aIn);  // read the input on analog pin 0:     
      float voltagereading = sensorValue*5/1024; 
      Serial.println(voltagereading);   // print out the value to serial port:
      //equation to take voltagereading to temp y = -93.68ln(x) + 168.33  (y=temp, x=voltage)
      double temp = (-93.68*log(voltagereading) + 168.33);
  
      display_me = temp;
      displayNumber(display_me); //keeps looping through to display the current temp

      loop_count++;

        if (0 == (loop_count%300))//every 300 ms
        {
          myFile = SD.open("test.txt", FILE_WRITE); //opens up a file on the SD named test.txt for writing
          myFile.println(temp); //prints to the file
          myFile.close(); //closes the file
        }
        
       if(temp<lowtemp)
       {
        digitalWrite(heatelement,HIGH);
       }
       else if(temp>hightemp)
       {
        digitalWrite(heatelement,LOW);
       }
              
     }
